// Logisim project PROCESSADOR_BIP Richard.circ as structural Verilog: 9 circuits, main circuit main
module main (
);

  wire caminho_controle_1_en_ram, caminho_controle_1_en_rom, caminho_controle_1_sel_op2,
       caminho_controle_1_sel_ula, caminho_controle_1_wr_acc, caminho_controle_1_wr_ram, caminho_dados_1_op0,
       caminho_dados_1_op1, caminho_dados_1_op2, caminho_dados_1_op3, CLOCK_out, Reset_2_out, RESET_out;
  wire [1:0] caminho_controle_1_sel_op1;
  wire [11:0] caminho_controle_1_add_rom, caminho_dados_1_add_ram;
  wire [15:0] caminho_dados_1_din_ram, ram_1_data, rom_1_data;

  Button RESET (.out(RESET_out));
  Clock CLOCK (.out(CLOCK_out));
  RAM #(.addrWidth(12), .dataWidth(16), .bus("separate")) ram_1 (
    .addr(caminho_dados_1_add_ram), .din(caminho_dados_1_din_ram), .data(ram_1_data),
    .str(caminho_controle_1_wr_ram), .sel(caminho_controle_1_en_ram), .clk(CLOCK_out), .ld(1'b1),
    .clr(RESET_out));
  ROM #(.addrWidth(12), .dataWidth(16)) rom_1 (
    .addr(caminho_controle_1_add_rom), .data(rom_1_data), .sel(caminho_controle_1_en_rom));
  CAMINHO_DADOS caminho_dados_1 (
    .CLOCK(CLOCK_out), .DOUT_RAM(ram_1_data), .DIN_RAM(caminho_dados_1_din_ram),
    .ADD_RAM(caminho_dados_1_add_ram), .SEL_ULA(caminho_controle_1_sel_ula),
    .WR_ACC(caminho_controle_1_wr_acc), .SEL_OP2(caminho_controle_1_sel_op2),
    .SEL_OP1(caminho_controle_1_sel_op1), .DOUT_ROM(rom_1_data), .OP0(caminho_dados_1_op0),
    .OP1(caminho_dados_1_op1), .OP2(caminho_dados_1_op2), .OP3(caminho_dados_1_op3));
  Button Reset_2 (.out(Reset_2_out));
  CAMINHO_CONTROLE caminho_controle_1 (
    .CLOCK(CLOCK_out), .RESET(Reset_2_out), .OP3(caminho_dados_1_op3), .OP2(caminho_dados_1_op2),
    .OP1(caminho_dados_1_op1), .OP0(caminho_dados_1_op0), .EN_ROM(caminho_controle_1_en_rom),
    .EN_RAM(caminho_controle_1_en_ram), .WR_RAM(caminho_controle_1_wr_ram),
    .WR_ACC(caminho_controle_1_wr_acc), .SEL_OP1(caminho_controle_1_sel_op1),
    .SEL_OP2(caminho_controle_1_sel_op2), .SEL_ULA(caminho_controle_1_sel_ula),
    .ADD_ROM(caminho_controle_1_add_rom));

  // Notes on the sheet:
  //   contents of rom_1 (hex, n*v repeats v):
  //   3015 1000 300a 1001 303f 1002 302a 1003 2000 4000 1004 2002 4002 4004 4003 6001 1005
endmodule

module ULA (
  input  [15:0] A,
  input  [15:0] B,
  input  SEL_ULA,
  output [15:0] S
);

  wire [15:0] adder_1_out, subtractor_1_out;

  Adder #(.width(16)) adder_1 (.a(A), .b(B), .out(adder_1_out));  // open: cin, cout
  Subtractor #(.width(16)) subtractor_1 (.a(A), .b(B), .out(subtractor_1_out));  // open: bin, bout
  Multiplexer #(.width(16), .enable("false")) multiplexer_1 (
    .in0(adder_1_out), .in1(subtractor_1_out), .out(S), .sel(SEL_ULA));
endmodule

// c_dados
module CAMINHO_DADOS (
  input  CLOCK,
  input  [15:0] DOUT_RAM,
  input  SEL_ULA,
  input  WR_ACC,
  input  SEL_OP2,
  input  [1:0] SEL_OP1,
  input  [15:0] DOUT_ROM,
  output [15:0] DIN_RAM,
  output [11:0] ADD_RAM,
  output OP0,
  output OP1,
  output OP2,
  output OP3
);

  wire [15:0] bit_extender_1_out, multiplexer_1_out, multiplexer_2_out, ula_1_s, undriven;

  Multiplexer #(.width(16), .enable("false")) multiplexer_1 (
    .in0(undriven), .in1(DOUT_RAM), .out(multiplexer_1_out), .sel(SEL_OP2));
  Multiplexer #(.select(2), .width(16), .enable("false")) multiplexer_2 (
    .in0(ula_1_s), .in1(bit_extender_1_out), .in2(DOUT_RAM), .in3(undriven), .out(multiplexer_2_out),
    .sel(SEL_OP1));
  assign bit_extender_1_out = {{4{1'b0}}, ADD_RAM};  // Bit_Extender bit_extender_1
  Register #(.width(16)) ACC (.D(multiplexer_2_out), .en(WR_ACC), .Q(DIN_RAM), .clk(CLOCK));  // open: clr
  ULA ula_1 (.A(DIN_RAM), .B(multiplexer_1_out), .SEL_ULA(SEL_ULA), .S(ula_1_s));
  Register #(.width(16)) IR (.D(DOUT_ROM), .en(1'b1), .Q({OP3, OP2, OP1, OP0, ADD_RAM}), .clk(CLOCK));  // open: clr
endmodule

// c_controle
module CAMINHO_CONTROLE (
  input  OP3,
  input  OP2,
  input  OP1,
  input  OP0,
  input  CLOCK,
  input  RESET,
  output EN_ROM,
  output EN_RAM,
  output WR_RAM,
  output WR_ACC,
  output [1:0] SEL_OP1,
  output SEL_OP2,
  output SEL_ULA,
  output [11:0] ADD_ROM
);

  wire logica_controle_1_en_pc;

  PROGRAMM_COUNTER PROGRAMM_COUNTER (.EN_PC(logica_controle_1_en_pc), .CLOCK(CLOCK), .ADD_ROM(ADD_ROM));
  LOGICA_CONTROLE logica_controle_1 (
    .OP3(OP3), .OP2(OP2), .OP1(OP1), .OP0(OP0), .EN_PC(logica_controle_1_en_pc), .EN_ROM(EN_ROM),
    .EN_RAM(EN_RAM), .WR_RAM(WR_RAM), .WR_ACC(WR_ACC), .SEL_OP1(SEL_OP1), .SEL_OP2(SEL_OP2), .SEL_ULA(SEL_ULA));
endmodule

module PROGRAMM_COUNTER (
  input  EN_PC,
  input  CLOCK,
  output [11:0] ADD_ROM
);

  wire RESET_out;
  wire [11:0] adder_1_out;

  Adder #(.width(12)) adder_1 (.a(ADD_ROM), .b(12'h1), .out(adder_1_out));  // open: cin, cout
  Register #(.width(12)) PC (.D(adder_1_out), .en(EN_PC), .Q(ADD_ROM), .clk(CLOCK), .clr(RESET_out));
  Button RESET (.out(RESET_out));
endmodule

// log_controle
module LOGICA_CONTROLE (
  input  OP3,
  input  OP2,
  input  OP1,
  input  OP0,
  output EN_PC,
  output EN_ROM,
  output EN_RAM,
  output WR_RAM,
  output WR_ACC,
  output [1:0] SEL_OP1,
  output SEL_OP2,
  output SEL_ULA
);

  wire not_1_out, not_2_out, not_3_out, not_4_out;

  SEL_OP1 sel_op1_1 (.OP3(OP3), .OP2(OP2), .OP1(OP1), .OP0(OP0), .SEL_OP1(SEL_OP1));
  SEL_OP2 sel_op2_1 (.OP3(OP3), .OP2(OP2), .OP0(OP0), .SEL_OP2(SEL_OP2));
  not not_1 (not_1_out, OP3);
  not not_2 (not_2_out, OP1);
  not not_3 (not_3_out, OP2);
  not not_4 (not_4_out, OP3);
  EN_RAM u_en_ram (.OP3(OP3), .OP2(OP2), .OP1(OP1), .OP0(OP0), .EN_RAM(EN_RAM));
  and and_1 (SEL_ULA, OP1, OP2, not_1_out);
  or or_1 (EN_PC, OP0, OP1, OP2, OP3);
  and and_2 (WR_RAM, OP0, not_2_out, not_3_out, not_4_out);
  or or_2 (WR_ACC, OP1, OP2, OP3);

  assign EN_ROM = EN_PC;
endmodule

module EN_RAM (
  input  OP3,
  input  OP2,
  input  OP1,
  input  OP0,
  output EN_RAM
);

  wire and_1_out, and_2_out, and_3_out, and_4_out, not_1_out, not_2_out, not_3_out, not_4_out, not_5_out,
       not_6_out, not_7_out, not_8_out, not_9_out, not_10_out, not_11_out;

  not not_1 (not_1_out, OP1);
  not not_2 (not_2_out, OP2);
  not not_3 (not_3_out, OP3);
  not not_4 (not_4_out, OP0);
  not not_5 (not_5_out, OP2);
  not not_6 (not_6_out, OP3);
  not not_7 (not_7_out, OP0);
  not not_8 (not_8_out, OP1);
  not not_9 (not_9_out, OP3);
  not not_10 (not_10_out, OP0);
  not not_11 (not_11_out, OP3);
  and and_1 (and_1_out, OP0, not_1_out, not_2_out, not_3_out);
  and and_2 (and_2_out, not_4_out, OP1, not_5_out, not_6_out);
  and and_3 (and_3_out, not_7_out, not_8_out, OP2, not_9_out);
  and and_4 (and_4_out, not_10_out, OP1, OP2, not_11_out);
  or or_1 (EN_RAM, and_1_out, and_2_out, and_3_out, and_4_out);
endmodule

// sel_op1
module SEL_OP1 (
  input  OP3,
  input  OP2,
  input  OP1,
  input  OP0,
  output [1:0] SEL_OP1
);

  wire not_1_out, not_2_out, not_3_out, not_4_out, not_5_out;

  not not_1 (not_1_out, OP2);
  not not_2 (not_2_out, OP3);
  not not_3 (not_3_out, OP0);
  not not_4 (not_4_out, OP2);
  not not_5 (not_5_out, OP3);
  and BIT0 (SEL_OP1[0], OP0, OP1, not_1_out, not_2_out);
  and BIT1 (SEL_OP1[1], not_3_out, OP1, not_4_out, not_5_out);
endmodule

// sel_op2
module SEL_OP2 (
  input  OP3,
  input  OP2,
  input  OP0,
  output SEL_OP2
);

  wire not_1_out, not_2_out;

  not not_1 (not_1_out, OP0);
  not not_2 (not_2_out, OP3);
  and and_1 (SEL_OP2, OP2, not_1_out, not_2_out);
endmodule
